# Fritzing sketch wiring (saved by Fritzing 0.9.2b)
breadboards: 2

parts:
  Part1 = Arduino Nano (Rev3.0)

nets:
  N1: Part1.GND, Part1.D9

notes:
  Suppy power via USB (cut open old cable) or apply 7-12V to VIN
  3-pin connector output 1
  3-pin connector output 2
  3-pin connector input flight controller
